// Logisim project CMOS_Logic.circ as structural Verilog: 1 circuit, main circuit main
module main (
  input  NOT,
  input  in_2,
  input  NAND,
  input  AND,
  input  in_5,
  input  in_6,
  input  in_7,
  input  AND__from_NAND,
  input  in_9,
  input  in_10,
  input  NOR,
  input  OR,
  input  in_13,
  input  in_14,
  input  NOR__from_NAND,
  input  in_16,
  input  in_17,
  input  in_18,
  output out_19,
  output out_20,
  output out_21,
  output out_22,
  output out_23,
  output out_24,
  output out_25,
  output out_26,
  output out_27,
  output out_28
);

  wire nand_4_out, nand_5_out, nand_6_out, nand_8_out, nand_9_out, nand_10_out, transistor_6_out,
       transistor_7_out, transistor_11_out, transistor_13_out, transistor_14_out, transistor_15_out;

  Transistor transistor_1 (.in(1'b1), .out(out_22), .gate(NAND));
  Transistor #(.\type ("n")) transistor_2 (.in(1'b0), .out(out_25), .gate(NOR));
  Transistor transistor_3 (.in(1'b1), .out(out_19), .gate(NOT));
  Transistor #(.\type ("n")) transistor_4 (.in(1'b0), .out(out_19), .gate(NOT));
  Transistor #(.\type ("n")) transistor_5 (.in(transistor_6_out), .out(out_22), .gate(NAND));
  Transistor #(.\type ("n")) transistor_6 (.in(1'b0), .out(transistor_6_out), .gate(in_6));
  Transistor transistor_7 (.in(1'b1), .out(transistor_7_out), .gate(NOR));
  Transistor transistor_8 (.in(transistor_7_out), .out(out_25), .gate(in_13));
  // NOT_Gate not_1 is placed but not wired
  // NAND_Gate nand_1 has open pins: in2=out_22, in3=out_22, out=open
  Transistor transistor_9 (.in(1'b1), .out(out_22), .gate(in_6));
  // NOR_Gate nor_1 is placed but not wired
  Transistor #(.\type ("n")) transistor_10 (.in(1'b0), .out(out_25), .gate(in_13));
  nand nand_2 (out_20, in_2, in_2, in_2);
  nand nand_3 (out_21, in_5, in_9);
  nand nand_4 (nand_4_out, NOR__from_NAND, NOR__from_NAND, NOR__from_NAND);
  nand nand_5 (nand_5_out, in_17, in_17, in_17);
  nand nand_6 (nand_6_out, nand_4_out, nand_5_out);
  nand nand_7 (out_27, nand_6_out, nand_6_out, nand_6_out);
  Transistor transistor_11 (.in(1'b1), .out(transistor_11_out), .gate(AND));
  Transistor #(.\type ("n")) transistor_12 (.in(transistor_13_out), .out(transistor_11_out), .gate(AND));
  Transistor #(.\type ("n")) transistor_13 (.in(1'b0), .out(transistor_13_out), .gate(in_7));
  Transistor transistor_14 (.in(1'b1), .out(transistor_14_out), .gate(OR));
  Transistor transistor_15 (.in(transistor_14_out), .out(transistor_15_out), .gate(in_14));
  Transistor #(.\type ("n")) transistor_16 (.in(1'b0), .out(transistor_15_out), .gate(OR));
  Transistor transistor_17 (.in(1'b1), .out(transistor_11_out), .gate(in_7));
  Transistor transistor_18 (.in(1'b1), .out(out_23), .gate(transistor_11_out));
  Transistor #(.\type ("n")) transistor_19 (.in(1'b0), .out(out_23), .gate(transistor_11_out));
  Transistor #(.\type ("n")) transistor_20 (.in(1'b0), .out(transistor_15_out), .gate(in_14));
  // AND_Gate and_1 is placed but not wired
  Transistor transistor_21 (.in(1'b1), .out(out_26), .gate(transistor_15_out));
  Transistor #(.\type ("n")) transistor_22 (.in(1'b0), .out(out_26), .gate(transistor_15_out));
  // OR_Gate or_1 is placed but not wired
  nand nand_8 (nand_8_out, AND__from_NAND, in_10);
  nand nand_9 (nand_9_out, in_16, in_16, in_16);
  nand nand_10 (nand_10_out, in_18, in_18, in_18);
  nand nand_11 (out_24, nand_8_out, nand_8_out, nand_8_out);
  nand nand_12 (out_28, nand_9_out, nand_10_out);

  // Notes on the sheet:
  //   NOT (from NAND)
  //   OR (from NAND)
endmodule
